// Logisim project project2.circ as structural Verilog: 1 circuit, main circuit main
module main (
  output MemRead,
  output MemWrite,
  output [7:0] RegData1,
  output [1:0] ReadReg1,
  output [7:0] RegData2,
  output [1:0] ReadReg2,
  output [1:0] WriteReg,
  output [7:0] RegDataW,
  output Imm2,
  output operation
);

  wire and_1_out, and_2_out, and_3_out, and_4_out, clock_1_out, clock_2_out, decoder_1_out0, decoder_1_out1,
       decoder_1_out2, decoder_1_out3;
  wire [3:0] multiplexer_1_out, multiplexer_1_out_2;
  wire [7:0] adder_1_out, adder_2_out, multiplexer_4_out, multiplexer_5_out, multiplexer_6_out, ram_2_dout,
       register_1_q, subtractor_1_out, X0_q, X1_q, X2_q, X3_q;
  wire [19:0] ram_1_dout;

  Adder adder_1 (.a(register_1_q), .b(8'h1), .out(adder_1_out));  // open: cin, cout
  Register register_1 (.D(adder_1_out), .en(1'b1), .clk(clock_1_out), .Q(register_1_q));  // open: clr
  Clock clock_1 (.out(clock_1_out));
  RAM #(.dataWidth(24), .enables("line")) ram_1 (
    .addr(register_1_q), .we(1'b0), .clk(clock_1_out),
    .dout({WriteReg, ReadReg1, ram_1_dout[19:14], ReadReg2, ram_1_dout[11:5], operation, MemWrite, MemRead, Imm2, ram_1_dout[0]}));  // open: din
  Decoder #(.select(2)) decoder_1 (
    .out0(decoder_1_out0), .out1(decoder_1_out1), .out2(decoder_1_out2), .out3(decoder_1_out3), .sel(WriteReg));  // open: en
  and and_1 (and_1_out, ram_1_dout[0], decoder_1_out0);
  and and_2 (and_2_out, ram_1_dout[0], decoder_1_out1);
  and and_3 (and_3_out, ram_1_dout[0], decoder_1_out2);
  and and_4 (and_4_out, ram_1_dout[0], decoder_1_out3);
  Register X0 (.D(multiplexer_6_out), .en(and_1_out), .clk(clock_1_out), .Q(X0_q));  // open: clr
  Register X1 (.D(multiplexer_6_out), .en(and_2_out), .clk(clock_1_out), .Q(X1_q));  // open: clr
  Register X2 (.D(multiplexer_6_out), .en(and_3_out), .clk(clock_1_out), .Q(X2_q));  // open: clr
  Register X3 (.D(multiplexer_6_out), .en(and_4_out), .clk(clock_1_out), .Q(X3_q));  // open: clr
  Hex_Digit_Display hex_digit_display_1 (.value(multiplexer_1_out_2));  // open: dp
  Hex_Digit_Display hex_digit_display_2 (.value(multiplexer_1_out));  // open: dp
  Multiplexer #(.width(8)) multiplexer_1 (
    .in1(multiplexer_5_out), .out({multiplexer_1_out_2, multiplexer_1_out}), .sel(ram_1_dout[5]));  // open: in0
  Multiplexer #(.select(2), .width(8)) multiplexer_2 (
    .in0(X0_q), .in1(X1_q), .in2(X2_q), .in3(X3_q), .out(RegData1), .sel(ReadReg1));
  Multiplexer #(.select(2), .width(8)) multiplexer_3 (
    .in0(X0_q), .in1(X1_q), .in2(X2_q), .in3(X3_q), .out(RegData2), .sel(ReadReg2));
  Multiplexer #(.width(8)) multiplexer_4 (
    .in0(RegData2), .in1({ram_1_dout[19:14], ReadReg2}), .out(multiplexer_4_out), .sel(Imm2));
  Adder adder_2 (.a(RegData1), .b(multiplexer_4_out), .out(adder_2_out));  // open: cin, cout
  Subtractor subtractor_1 (.a(RegData1), .b(multiplexer_4_out), .out(subtractor_1_out));  // open: bin, bout
  Multiplexer #(.width(8)) multiplexer_5 (
    .in0(adder_2_out), .in1(subtractor_1_out), .out(multiplexer_5_out), .sel(operation));
  Multiplexer #(.width(8)) multiplexer_6 (
    .in0(multiplexer_5_out), .in1(ram_2_dout), .out(multiplexer_6_out), .sel(MemRead));
  RAM #(.enables("line")) ram_2 (
    .addr(multiplexer_4_out), .we(MemWrite), .clk(clock_2_out), .din(RegData1), .dout(ram_2_dout));
  Clock clock_2 (.out(clock_2_out));

  // Notes on the sheet:
  //   Instruction
  //   Intel ® Core ™ i(negative)5
  //   Name: Amane Chibana and Harry Wang
  //   Pledge: I pledge my honor that I have abided by the Stevens Honor System.
  //   ALU
  //   Memory
endmodule
